// Logisim project RegisterFile&ALU.circ as structural Verilog: 7 circuits, main circuit main
module main (
  input  Write_Enable,
  input  [31:0] _32bit_Instruction,
  output out_3,
  output out_4
);

  wire clock_1_out;
  wire [4:0] splitter_1_p3, splitter_1_p4, splitter_1_p5, splitter_1_p6;
  wire [5:0] func, splitter_1_p2;
  wire [15:0] alu_1_mux1_res, registerfile_1_read_data1, registerfile_1_read_data2;

  // Splitter splitter_1: pin names not known; wires that end beside it: _32bit_Instruction, splitter_1_p2, splitter_1_p3, splitter_1_p4, splitter_1_p5, splitter_1_p6, func
  RegisterFile registerfile_1 (
    .Write_Data(alu_1_mux1_res), .Write_Enable(Write_Enable), .in_4(splitter_1_p3[3:0]),
    .Read_Address1(splitter_1_p4[3:0]), .Read_Address2(splitter_1_p5[3:0]), .in_2(clock_1_out),
    .Read_Data1(registerfile_1_read_data1), .Read_Data2(registerfile_1_read_data2));
  Clock clock_1 (.out(clock_1_out));
  ALU alu_1 (
    .shamt(splitter_1_p6), .Input_A(registerfile_1_read_data1), .opcode(splitter_1_p2),
    .Input_B(registerfile_1_read_data2), .opcode_2(splitter_1_p2), .carryout(out_4), .overflow(out_3),
    .mux1_res(alu_1_mux1_res));

  // Notes on the sheet:
  //   rd
  //   rs
  //   rt
  //   opcode
  //   shamt
endmodule

module onebitAdder (
  input  A,
  input  B,
  input  Cin,
  output S,
  output Cout
);

  wire and_1_out, and_2_out, xor_1_out;

  xor xor_1 (xor_1_out, A, B);
  and and_1 (and_1_out, Cin, xor_1_out);
  and and_2 (and_2_out, B, A);
  xor xor_2 (S, xor_1_out, Cin);
  or or_1 (Cout, and_1_out, and_2_out);
endmodule

module ALU (
  input  [4:0] shamt,
  input  [15:0] Input_A,
  input  [5:0] opcode,
  input  [15:0] Input_B,
  input  [5:0] opcode_2,
  output [15:0] mux1_res,
  output overflow,
  output carryout
);

  wire carry_out_add, carry_out_addi, carry_out_sub, clock_1_out, decoder_1_out0, decoder_1_out1,
       decoder_1_out2, decoder_1_out4, enable, of_add, of_addi, of_sub, xor_1_out, xor_2_out, xor_3_out;
  wire [0:0] SLT;
  wire [15:0] Add, Addi, And, Hi, Lo, multiplier_1_cout, multiplier_1_out, Or, SLL, Sub;

  Shifter #(.width(16)) shifter_1 (.in(Input_A), .\dist (shamt[3:0]), .out(SLL));
  Multiplier #(.width(16)) multiplier_1 (
    .a(Input_A), .b(Input_B), .out(multiplier_1_out), .cout(multiplier_1_cout));  // open: cin
  assign And = Input_A & Input_B;  // AND_Gate AND, 16 bits wide
  assign Or = Input_A | Input_B;  // OR_Gate OR, 16 bits wide
  _16bitAdder u_16bitadder_1 (.Cin(1'b0), .in_2(Input_A), .in_3(Input_B), .out_4(carry_out_addi), .out_5(Addi));
  Subtractor #(.width(16)) subtractor_1 (.a(Input_A), .b(Input_B), .out(Sub), .bout(carry_out_sub));  // open: bin
  Comparator #(.width(16)) comparator_1 (.a(Input_A), .b(Input_B), .lt(SLT[0]));  // open: gt, eq
  _16bitAdder u_16bitadder_2 (.Cin(1'b0), .in_2(Input_A), .in_3(Input_B), .out_4(carry_out_add), .out_5(Add));
  Register #(.width(16)) Low (.D(multiplier_1_out), .Q(Lo), .clk(clock_1_out), .clr(decoder_1_out2));  // open: en
  nor nor_1 (enable, opcode_2[4], opcode_2[5]);
  Clock clock_1 (.out(clock_1_out));
  Register #(.width(16)) High (.D(multiplier_1_cout), .Q(Hi), .clk(clock_1_out), .clr(decoder_1_out2));  // open: en
  Decoder #(.select(4)) decoder_1 (
    .out0(decoder_1_out0), .out1(decoder_1_out1), .out2(decoder_1_out2), .out4(decoder_1_out4),
    .sel(opcode[3:0]), .en(enable));  // open: out3, out5, out6, out7, out8, out9, out10, out11, out12, out13, out14, out15
  Multiplexer #(.select(4), .width(16)) multiplexer_1 (
    .in0(Add), .in1(Sub), .in3(And), .in4(Or), .in5(Addi), .in6(SLL), .in7({{15{1'b0}}, SLT[0]}), .in8(Hi),
    .in9(Lo), .out(mux1_res), .sel(opcode[3:0]), .en(enable));  // open: in2, in10, in11, in12, in13, in14, in15
  Multiplexer #(.select(4)) multiplexer_2 (
    .in0(carry_out_add), .in1(carry_out_sub), .in5(carry_out_addi), .out(carryout), .sel(opcode[3:0]),
    .en(enable));  // open: in2, in3, in4, in6, in7, in8, in9, in10, in11, in12, in13, in14, in15
  xor xor_1 (xor_1_out, Input_A[15], Input_B[15]);
  xor xor_2 (xor_2_out, Input_A[15], Input_B[15]);
  xor xor_3 (xor_3_out, Input_A[15], Input_B[15]);
  Multiplexer multiplexer_3 (.in0(xor_1_out), .in1(1'b0), .out(of_add), .sel(decoder_1_out0), .en(enable));
  Multiplexer multiplexer_4 (.in0(xor_2_out), .in1(1'b0), .out(of_sub), .sel(decoder_1_out1), .en(enable));
  Multiplexer multiplexer_5 (.in0(xor_3_out), .in1(1'b0), .out(of_addi), .sel(decoder_1_out4), .en(enable));
  Multiplexer #(.select(4)) multiplexer_6 (
    .in0(of_add), .in1(of_sub), .in5(of_addi), .out(overflow), .sel(opcode[3:0]), .en(enable));  // open: in2, in3, in4, in6, in7, in8, in9, in10, in11, in12, in13, in14, in15

  // Other names for the same wires on the sheet: A[15:0] = Input_A; B[15:0] = Input_B; last_A = Input_A[15];
  //   last_B = Input_B[15]; opcode_t[3:0] = opcode[3:0]; shamt_t[3:0] = shamt[3:0]
endmodule

// Add
module _16bitAdder (
  input  Cin,
  input  [15:0] in_2,
  input  [15:0] in_3,
  output out_4,
  output [15:0] out_5
);

  wire onebitadder_2_cout, onebitadder_3_cout, onebitadder_4_cout, onebitadder_5_cout, onebitadder_6_cout,
       onebitadder_7_cout, onebitadder_8_cout, onebitadder_9_cout, onebitadder_10_cout, onebitadder_11_cout,
       onebitadder_12_cout, onebitadder_13_cout, onebitadder_14_cout, onebitadder_15_cout,
       onebitadder_16_cout;

  onebitAdder onebitadder_1 ();  // open: A, B, Cin, S, Cout
  onebitAdder onebitadder_2 (.A(in_3[0]), .B(in_2[0]), .Cin(Cin), .S(out_5[0]), .Cout(onebitadder_2_cout));
  onebitAdder onebitadder_3 (
    .A(in_3[1]), .B(in_2[1]), .Cin(onebitadder_2_cout), .S(out_5[1]), .Cout(onebitadder_3_cout));
  onebitAdder onebitadder_4 (
    .A(in_3[2]), .B(in_2[2]), .Cin(onebitadder_3_cout), .S(out_5[2]), .Cout(onebitadder_4_cout));
  onebitAdder onebitadder_5 (
    .A(in_3[3]), .B(in_2[3]), .Cin(onebitadder_4_cout), .S(out_5[3]), .Cout(onebitadder_5_cout));
  onebitAdder onebitadder_6 (
    .A(in_3[4]), .B(in_2[4]), .Cin(onebitadder_5_cout), .S(out_5[4]), .Cout(onebitadder_6_cout));
  onebitAdder onebitadder_7 (
    .A(in_3[5]), .B(in_2[5]), .Cin(onebitadder_6_cout), .S(out_5[5]), .Cout(onebitadder_7_cout));
  onebitAdder onebitadder_8 (
    .A(in_3[6]), .B(in_2[6]), .Cin(onebitadder_7_cout), .S(out_5[6]), .Cout(onebitadder_8_cout));
  onebitAdder onebitadder_9 (
    .A(in_3[7]), .B(in_2[7]), .Cin(onebitadder_8_cout), .S(out_5[7]), .Cout(onebitadder_9_cout));
  onebitAdder onebitadder_10 (
    .A(in_3[8]), .B(in_2[8]), .Cin(onebitadder_9_cout), .S(out_5[8]), .Cout(onebitadder_10_cout));
  onebitAdder onebitadder_11 (
    .A(in_3[9]), .B(in_2[9]), .Cin(onebitadder_10_cout), .S(out_5[9]), .Cout(onebitadder_11_cout));
  onebitAdder onebitadder_12 (
    .A(in_3[10]), .B(in_2[10]), .Cin(onebitadder_11_cout), .S(out_5[10]), .Cout(onebitadder_12_cout));
  onebitAdder onebitadder_13 (
    .A(in_3[11]), .B(in_2[11]), .Cin(onebitadder_12_cout), .S(out_5[11]), .Cout(onebitadder_13_cout));
  onebitAdder onebitadder_14 (
    .A(in_3[12]), .B(in_2[12]), .Cin(onebitadder_13_cout), .S(out_5[12]), .Cout(onebitadder_14_cout));
  onebitAdder onebitadder_15 (
    .A(in_3[13]), .B(in_2[13]), .Cin(onebitadder_14_cout), .S(out_5[13]), .Cout(onebitadder_15_cout));
  onebitAdder onebitadder_16 (
    .A(in_3[14]), .B(in_2[14]), .Cin(onebitadder_15_cout), .S(out_5[14]), .Cout(onebitadder_16_cout));
  onebitAdder onebitadder_17 (.A(in_3[15]), .B(in_2[15]), .Cin(onebitadder_16_cout), .S(out_5[15]), .Cout(out_4));

  // Other names for the same wires on the sheet: A0 = in_2[0]; A1 = in_2[1]; A2 = in_2[2]; A3 = in_2[3]; A4 = in_2[4];
  //   A5 = in_2[5]; A6 = in_2[6]; A7 = in_2[7]; A8 = in_2[8]; A9 = in_2[9]; A10 = in_2[10]; A11 = in_2[11];
  //   A12 = in_2[12]; A13 = in_2[13]; A14 = in_2[14]; A15 = in_2[15]; B0 = in_3[0]; B1 = in_3[1]; B2 = in_3[2];
  //   B3 = in_3[3]; B4 = in_3[4]; B5 = in_3[5]; B6 = in_3[6]; B7 = in_3[7]; B8 = in_3[8]; B9 = in_3[9];
  //   B10 = in_3[10]; B11 = in_3[11]; B12 = in_3[12]; B13 = in_3[13]; B14 = in_3[14]; B15 = in_3[15]

  // Notes on the sheet:
  //   A
  //   B
  //   Sol
  //   Cout
endmodule

module Splitter (
  input  [31:0] in_1,
  output [5:0] op,
  output [4:0] rd,
  output [4:0] rs,
  output [4:0] rt,
  output [4:0] sh,
  output [5:0] funct,
  output [15:0] imm
);


  assign funct = in_1[5:0];
  assign imm = in_1[15:0];
  assign op = in_1[31:26];
  assign rd = in_1[25:21];
  assign rs = in_1[20:16];
  assign rt = in_1[15:11];
  assign sh = in_1[10:6];

  // Other names for the same wires on the sheet: func[5:0] = in_1[5:0]; Immediate[15:0] = in_1[15:0];
  //   opcode[5:0] = in_1[31:26]; shamt[4:0] = in_1[10:6]
endmodule

module RegisterFile (
  input  [15:0] Write_Data,
  input  in_2,
  input  Write_Enable,
  input  [3:0] in_4,
  input  [3:0] Read_Address1,
  input  [3:0] Read_Address2,
  output [15:0] Read_Data1,
  output [15:0] Read_Data2
);

  wire and_1_out, and_2_out, and_3_out, and_4_out, and_5_out, and_6_out, and_7_out, and_8_out, and_9_out,
       and_10_out, and_11_out, and_12_out, and_13_out, and_14_out, and_15_out, and_16_out, Clock_prime,
       decoder_1_out0, decoder_1_out1, decoder_1_out2, decoder_1_out3, decoder_1_out4, decoder_1_out5,
       decoder_1_out6, decoder_1_out7, decoder_1_out8, decoder_1_out9, decoder_1_out10, decoder_1_out11,
       decoder_1_out12, decoder_1_out13, decoder_1_out14, decoder_1_out15;
  wire [15:0] R0, R1, R2, R3, R4, R5, R6, R7, R8, R9, R10, R11, R12, R13, R14, R15;

  Decoder #(.select(4)) decoder_1 (
    .out0(decoder_1_out0), .out1(decoder_1_out1), .out2(decoder_1_out2), .out3(decoder_1_out3),
    .out4(decoder_1_out4), .out5(decoder_1_out5), .out6(decoder_1_out6), .out7(decoder_1_out7),
    .out8(decoder_1_out8), .out9(decoder_1_out9), .out10(decoder_1_out10), .out11(decoder_1_out11),
    .out12(decoder_1_out12), .out13(decoder_1_out13), .out14(decoder_1_out14), .out15(decoder_1_out15),
    .sel(in_4));  // open: en
  Multiplexer #(.select(4), .width(16)) multiplexer_1 (
    .in0(R0), .in1(R1), .in2(R2), .in3(R3), .in4(R4), .in5(R5), .in6(R6), .in7(R7), .in8(R8), .in9(R9),
    .in10(R10), .in11(R11), .in12(R12), .in13(R13), .in14(R14), .in15(R15), .out(Read_Data1),
    .sel(Read_Address1), .en(Clock_prime));
  and and_1 (and_1_out, decoder_1_out0, Write_Enable);
  and and_2 (and_2_out, decoder_1_out1, Write_Enable);
  and and_3 (and_3_out, decoder_1_out2, Write_Enable);
  and and_4 (and_4_out, decoder_1_out3, Write_Enable);
  not not_1 (Clock_prime, in_2);
  Register #(.width(16)) u_R0 (.D(Write_Data), .en(and_1_out), .Q(R0), .clr(in_2));  // open: clk
  Register #(.width(16)) u_R1 (.D(Write_Data), .en(and_2_out), .clr(in_2));  // open: Q, clk
  Register #(.width(16)) u_R2 (.D(Write_Data), .en(and_3_out), .Q(R2), .clr(in_2));  // open: clk
  Register #(.width(16)) u_R3 (.D(Write_Data), .en(and_4_out), .Q(R3), .clk(in_2));  // open: clr
  and and_5 (and_5_out, decoder_1_out4, Write_Enable);
  and and_6 (and_6_out, decoder_1_out5, Write_Enable);
  and and_7 (and_7_out, decoder_1_out6, Write_Enable);
  and and_8 (and_8_out, decoder_1_out7, Write_Enable);
  Register #(.width(16)) u_R4 (.D(Write_Data), .en(and_5_out), .Q(R4), .clk(in_2));  // open: clr
  Register #(.width(16)) u_R5 (.D(Write_Data), .en(and_6_out), .Q(R5), .clk(in_2));  // open: clr
  Register #(.width(16)) u_R6 (.D(Write_Data), .en(and_7_out), .Q(R6), .clk(in_2));  // open: clr
  Register #(.width(16)) u_R7 (.D(Write_Data), .en(and_8_out), .Q(R7), .clk(in_2));  // open: clr
  and and_9 (and_9_out, decoder_1_out8, Write_Enable);
  and and_10 (and_10_out, decoder_1_out9, Write_Enable);
  and and_11 (and_11_out, decoder_1_out10, Write_Enable);
  and and_12 (and_12_out, decoder_1_out11, Write_Enable);
  Register #(.width(16)) u_R8 (.D(Write_Data), .en(and_9_out), .Q(R8), .clk(in_2));  // open: clr
  Register #(.width(16)) u_R9 (.D(Write_Data), .en(and_10_out), .Q(R9), .clk(in_2));  // open: clr
  Register #(.width(16)) u_R10 (.D(Write_Data), .en(and_11_out), .Q(R10), .clk(in_2));  // open: clr
  Register #(.width(16)) u_R11 (.D(Write_Data), .en(and_12_out), .Q(R11), .clk(in_2));  // open: clr
  Multiplexer #(.select(4), .width(16)) multiplexer_2 (
    .in0(R0), .in1(R1), .in2(R2), .in3(R3), .in4(R4), .in5(R5), .in6(R6), .in7(R7), .in8(R8), .in9(R9),
    .in10(R10), .in11(R11), .in12(R12), .in13(R13), .in14(R14), .in15(R15), .out(Read_Data2),
    .sel(Read_Address2), .en(Clock_prime));
  and and_13 (and_13_out, decoder_1_out12, Write_Enable);
  and and_14 (and_14_out, decoder_1_out13, Write_Enable);
  and and_15 (and_15_out, decoder_1_out14, Write_Enable);
  and and_16 (and_16_out, decoder_1_out15, Write_Enable);
  Register #(.width(16)) u_R12 (.D(Write_Data), .en(and_13_out), .Q(R12), .clk(in_2));  // open: clr
  Register #(.width(16)) u_R13 (.D(Write_Data), .en(and_14_out), .Q(R13), .clk(in_2));  // open: clr
  Register #(.width(16)) u_R14 (.D(Write_Data), .en(and_15_out), .Q(R14), .clk(in_2));  // open: clr
  Register #(.width(16)) u_R15 (.D(Write_Data), .en(and_16_out), .Q(R15), .clk(in_2));  // open: clr

  // Other names for the same wires on the sheet: Clock = in_2

  // Notes on the sheet:
  //   Write Address
endmodule

module InstructionFetch (
);

  wire and_1_out, Branch, CLK, Jump, Zero;
  wire [4:0] rd, rs, rt, shamt;
  wire [5:0] funct, Opcode;
  wire [15:0] adder_1_out, adder_2_out, immediate, multiplexer_1_out, multiplexer_2_out, register_1_q,
       shifter_1_out;
  wire [31:0] rom_1_data;

  Clock Clock (.out(CLK));
  Register #(.width(16)) register_1 (.D(multiplexer_2_out), .Q(register_1_q), .clk(CLK));  // open: en, clr
  Adder #(.width(16)) adder_1 (.a(register_1_q), .b(16'h1), .out(adder_1_out));  // open: cin, cout
  Shifter #(.width(16)) shifter_1 (.in(immediate), .\dist (4'b0010), .out(shifter_1_out));
  Adder #(.width(16)) adder_2 (.a(adder_1_out), .b(shifter_1_out), .out(adder_2_out));  // open: cin, cout
  ROM #(.addrWidth(16), .dataWidth(32)) rom_1 (.addr(register_1_q), .data(rom_1_data));  // open: sel
  Multiplexer #(.width(16), .enable("false")) multiplexer_1 (
    .in0(adder_1_out), .in1(adder_2_out), .out(multiplexer_1_out), .sel(and_1_out));
  and and_1 (and_1_out, Branch, Zero);
  // Splitter splitter_1: pin names not known; wires that end beside it: rom_1_data, Opcode, rd, rs, rt, shamt, funct, immediate
  Multiplexer #(.width(16), .enable("false")) multiplexer_2 (
    .in0(multiplexer_1_out), .in1(immediate), .out(multiplexer_2_out), .sel(Jump));

  // Notes on the sheet:
  //   contents of rom_1 (hex, n*v repeats v):
  //   4085800 4085800 b313280 d56ffc0 10f503f3 166607f9 1b0a782b 1c29e55e 23f001f0 24d67fe0 2b350ff0
  //   2ffd0033 3301ff83 359903f1 39ca003f 3c8affea
endmodule
